# Fritzing sketch HardwareConnections (saved by Fritzing 0.9.3b)

parts:
  Part1 = 9-DOF Absolute Orientation IMU Fusion Breakout - BNO055
  SparkFun_ESP32_Thing1 = SparkFun ESP32 Thing [part_number=DEV-13907]
  U1 = LIPO-1000mAh [package=lipo-1000]

nets:
  N1: Part1.5.0V, SparkFun_ESP32_Thing1.3.3V
  GND: Part1.GND, SparkFun_ESP32_Thing1.GND, U1.-
  N2: Part1.SDA_5V, SparkFun_ESP32_Thing1.21
  N3: Part1.SCL_5V, SparkFun_ESP32_Thing1.22
  N4: SparkFun_ESP32_Thing1.V_BATT, U1.+

custom parts:
  9-DOF Absolute Orientation IMU Fusion Breakout - BNO055: A MEMS accelerometer, magnetometer and gyroscope on a single die with a high speed ARM Cortex-M0 based processor to digest all the sensor data, abstract the sensor fusion and real time requirements away, and spit out data you can use in quaternions, Euler angles or vectors.
  SparkFun ESP32 Thing: The SparkFun ESP32 Thing is a comprehensive development platform for Espressif’s ESP32, their super-charged version of the popular ESP8266. Like the 8266, the ESP32 is a WiFi-compatible microcontroller, but to that it adds support for Bluetooth low-energy (i.e BLE, BT4.0, Bluetooth Smart), and nearly 30 I/O pins. The ESP32’s power and versatility will make it the foundation of IoT and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
